// Logisim project 7 seg.circ as structural Verilog: 1 circuit, main circuit main
module main (
  input  b3,
  input  b2,
  input  b1,
  input  b0
);

  wire and_1_out, and_2_out, and_3_out, and_4_out, and_5_out, and_6_out, and_7_out, and_8_out, and_9_out,
       and_10_out, not_1_out, not_2_out, not_3_out, not_4_out, not_5_out, not_6_out, not_7_out, not_8_out,
       not_9_out, not_10_out, not_11_out, not_12_out, not_13_out, not_14_out, not_15_out, or_1_out, or_2_out,
       or_3_out, or_4_out, or_5_out, or_6_out, or_7_out, xnor_1_out, xnor_2_out, xor_1_out;

  not not_1 (not_1_out, b0);
  not not_2 (not_2_out, b0);
  not not_3 (not_3_out, b1);
  not not_4 (not_4_out, b1);
  not not_5 (not_5_out, b0);
  not not_6 (not_6_out, b0);
  not not_7 (not_7_out, b0);
  not not_8 (not_8_out, b2);
  not not_9 (not_9_out, b1);
  not not_10 (not_10_out, b0);
  not not_11 (not_11_out, b0);
  not not_12 (not_12_out, b2);
  not not_13 (not_13_out, b2);
  xnor xnor_1 (xnor_1_out, b0, b1);
  xnor xnor_2 (xnor_2_out, b0, b2);
  and and_1 (and_1_out, not_1_out, b2);
  and and_2 (and_2_out, not_2_out, not_3_out);
  and and_3 (and_3_out, not_4_out, b2);
  xor xor_1 (xor_1_out, b1, b2);
  and and_4 (and_4_out, not_5_out, b2);
  and and_5 (and_5_out, not_6_out, b1);
  and and_6 (and_6_out, not_7_out, not_8_out);
  and and_7 (and_7_out, b0, not_9_out, b2);
  and and_8 (and_8_out, not_10_out, b1);
  and and_9 (and_9_out, not_11_out, not_12_out);
  and and_10 (and_10_out, b1, not_13_out);
  or or_1 (or_1_out, xnor_1_out, not_14_out, b3);
  not not_14 (not_14_out, b2);
  or or_2 (or_2_out, xnor_2_out, b1, b3);
  or or_3 (or_3_out, and_1_out, and_2_out, and_3_out, b3);
  or or_4 (or_4_out, xor_1_out, and_4_out, b3);
  or or_5 (or_5_out, and_5_out, and_6_out);
  or or_6 (or_6_out, and_7_out, and_8_out, and_9_out, and_10_out, b3);
  or or_7 (or_7_out, b0, not_15_out, b2);
  not not_15 (not_15_out, b1);
  _7_Segment_Display u_7_segment_display_1 (
    .g(or_4_out), .f(or_3_out), .a(or_2_out), .b(or_1_out), .e(or_5_out), .d(or_6_out), .c(or_7_out));  // open: dp

  // Notes on the sheet:
  //   7 Segment Display
  //   b
  //   a
  //   f
  //   g
  //   e
  //   d
  //   c
  //   b
  //   a
  //   f
  //   g
  //   e
  //   c
  //   d
endmodule
