// Logisim project All.circ as structural Verilog: 10 circuits, main circuit main
module main (
);


  // Notes on the sheet:
  //   Registers - Left Shift, Right Shift, Universal Shift, Arithmetic Shift, Logical shift
endmodule

module D_Flip_Flop (
  input  D,
  output Q,
  output Q_prime
);

  wire clock_1_out, nand_1_out, nand_2_out, not_1_out;

  Clock clock_1 (.out(clock_1_out));
  not not_1 (not_1_out, D);
  nand nand_1 (nand_1_out, D, clock_1_out);
  nand nand_2 (nand_2_out, clock_1_out, not_1_out);
  nand nand_3 (Q, nand_1_out, Q_prime);
  nand nand_4 (Q_prime, Q, nand_2_out);
endmodule

module Register (
  input  A3,
  input  A2,
  input  A1,
  input  A0,
  output B3,
  output B2,
  output B1,
  output B0
);

  wire C_out;

  Clock C (.out(C_out));
  D_Flip_Flop_part d_ff_1 (.clk(C_out), .D(A3), .Q(B3));  // open: Qn, preset, en, reset
  D_Flip_Flop_part d_ff_2 (.clk(C_out), .D(A2), .Q(B2));  // open: Qn, preset, en, reset
  D_Flip_Flop_part d_ff_3 (.clk(C_out), .D(A1), .Q(B1));  // open: Qn, preset, en, reset
  D_Flip_Flop_part d_ff_4 (.clk(C_out), .D(A0), .Q(B0));  // open: Qn, preset, en, reset
endmodule

module Left_Shift (
  input  serial_input,
  output out_2,
  output out_3,
  output out_4,
  output out_5
);

  wire clock_1_out;

  Clock clock_1 (.out(clock_1_out));
  D_Flip_Flop_part d_ff_1 (.clk(clock_1_out), .D(out_3), .Q(out_2));  // open: Qn, preset, en, reset
  D_Flip_Flop_part d_ff_2 (.clk(clock_1_out), .D(out_4), .Q(out_3));  // open: Qn, preset, en, reset
  D_Flip_Flop_part d_ff_3 (.clk(clock_1_out), .D(out_5), .Q(out_4));  // open: Qn, preset, en, reset
  D_Flip_Flop_part d_ff_4 (.clk(clock_1_out), .D(serial_input), .Q(out_5));  // open: Qn, preset, en, reset
endmodule

module PIPO (
  input  D0,
  input  D1,
  input  D2,
  input  D3,
  output Q0,
  output Q1,
  output Q2,
  output Q3
);

  wire CLK_out;

  Clock CLK (.out(CLK_out));
  D_Flip_Flop_part FF0 (.clk(CLK_out), .D(D0), .Q(Q0));  // open: Qn, preset, en, reset
  D_Flip_Flop_part FF1 (.clk(CLK_out), .D(D1), .Q(Q1));  // open: Qn, preset, en, reset
  D_Flip_Flop_part FF2 (.clk(CLK_out), .D(D2), .Q(Q2));  // open: Qn, preset, en, reset
  D_Flip_Flop_part FF3 (.clk(CLK_out), .D(D3), .Q(Q3));  // open: Qn, preset, en, reset
endmodule

module PISO (
  input  B0,
  input  B1,
  input  B2,
  input  B3,
  input  Shift_Load,
  output Output
);

  wire _1_2_out, _1_out, _2_2_out, _2_out, _3_2_out, _3_out, _4_out, _5_out, _6_out, CLK_out, FF0_q, FF1_q,
       FF2_q, not_1_out;

  not not_1 (not_1_out, Shift_Load);
  Clock CLK (.out(CLK_out));
  and _1 (_1_out, FF0_q, Shift_Load);
  D_Flip_Flop_part FF0 (.clk(CLK_out), .D(B0), .Q(FF0_q));  // open: Qn, preset, en, reset
  and _2 (_2_out, not_1_out, B1);
  or _1_2 (_1_2_out, _1_out, _2_out);
  and _3 (_3_out, FF1_q, Shift_Load);
  or _2_2 (_2_2_out, _3_out, _4_out);
  D_Flip_Flop_part FF1 (.clk(CLK_out), .D(_1_2_out), .Q(FF1_q));  // open: Qn, preset, en, reset
  and _4 (_4_out, not_1_out, B2);
  and _5 (_5_out, FF2_q, Shift_Load);
  D_Flip_Flop_part FF2 (.clk(CLK_out), .D(_2_2_out), .Q(FF2_q));  // open: Qn, preset, en, reset
  and _6 (_6_out, not_1_out, B3);
  or _3_2 (_3_2_out, _5_out, _6_out);
  D_Flip_Flop_part FF3 (.clk(CLK_out), .D(_3_2_out), .Q(Output));  // open: Qn, preset, en, reset
endmodule

module SIPO (
  input  INPUT,
  output Q3,
  output Q2,
  output Q1,
  output Q0
);

  wire CLK_out;

  Clock CLK (.out(CLK_out));
  D_Flip_Flop_part FF3 (.clk(CLK_out), .D(INPUT), .Q(Q3));  // open: Qn, preset, en, reset
  D_Flip_Flop_part FF2 (.clk(CLK_out), .D(Q3), .Q(Q2));  // open: Qn, preset, en, reset
  D_Flip_Flop_part FF1 (.clk(CLK_out), .D(Q2), .Q(Q1));  // open: Qn, preset, en, reset
  D_Flip_Flop_part FF0 (.clk(CLK_out), .D(Q1), .Q(Q0));  // open: Qn, preset, en, reset
endmodule

module SISO (
  input  INPUT,
  output OUTPUT
);

  wire CLK_out, FF1_q, FF2_q, FF3_q;

  Clock CLK (.out(CLK_out));
  D_Flip_Flop_part FF3 (.clk(CLK_out), .D(INPUT), .Q(FF3_q));  // open: Qn, preset, en, reset
  D_Flip_Flop_part FF2 (.clk(CLK_out), .D(FF3_q), .Q(FF2_q));  // open: Qn, preset, en, reset
  D_Flip_Flop_part FF1 (.clk(CLK_out), .D(FF2_q), .Q(FF1_q));  // open: Qn, preset, en, reset
  D_Flip_Flop_part FF0 (.clk(CLK_out), .D(FF1_q), .Q(OUTPUT));  // open: Qn, preset, en, reset
endmodule

module Universal_Register (
  input  serial_input,
  input  in_2,
  input  in_3,
  input  in_4,
  input  in_5,
  input  serial_input_2,
  input  [1:0] in_7,
  output out_8,
  output out_9,
  output out_10,
  output out_11
);

  wire clock_1_out, multiplexer_1_out, multiplexer_2_out, multiplexer_3_out, multiplexer_4_out;

  Clock clock_1 (.out(clock_1_out));
  Multiplexer #(.select(2)) multiplexer_1 (
    .in0(out_8), .in1(serial_input), .in2(out_9), .in3(in_2), .out(multiplexer_1_out), .sel(in_7));  // open: en
  Multiplexer #(.select(2)) multiplexer_2 (
    .in0(out_9), .in1(out_8), .in2(out_10), .in3(in_3), .out(multiplexer_2_out), .sel(in_7));  // open: en
  Multiplexer #(.select(2)) multiplexer_3 (
    .in0(out_10), .in1(out_9), .in2(out_11), .in3(in_4), .out(multiplexer_3_out), .sel(in_7));  // open: en
  Multiplexer #(.select(2)) multiplexer_4 (
    .in0(out_11), .in1(out_10), .in2(serial_input_2), .in3(in_5), .out(multiplexer_4_out), .sel(in_7));  // open: en
  D_Flip_Flop_part d_ff_1 (.clk(clock_1_out), .D(multiplexer_1_out), .Q(out_8));  // open: Qn, preset, en, reset
  D_Flip_Flop_part d_ff_2 (.clk(clock_1_out), .D(multiplexer_2_out), .Q(out_9));  // open: Qn, preset, en, reset
  D_Flip_Flop_part d_ff_3 (.clk(clock_1_out), .D(multiplexer_3_out), .Q(out_10));  // open: Qn, preset, en, reset
  D_Flip_Flop_part d_ff_4 (.clk(clock_1_out), .D(multiplexer_4_out), .Q(out_11));  // open: Qn, preset, en, reset
endmodule

module Right_Shift (
  input  A,
  output out_2,
  output out_3,
  output out_4,
  output out_5
);

  wire clock_1_out;

  Clock clock_1 (.out(clock_1_out));
  D_Flip_Flop_part d_ff_1 (.clk(clock_1_out), .D(out_3), .Q(out_2));  // open: Qn, preset, en, reset
  D_Flip_Flop_part d_ff_2 (.clk(clock_1_out), .D(out_4), .Q(out_3));  // open: Qn, preset, en, reset
  D_Flip_Flop_part d_ff_3 (.clk(clock_1_out), .D(out_5), .Q(out_4));  // open: Qn, preset, en, reset
  D_Flip_Flop_part d_ff_4 (.clk(clock_1_out), .D(A), .Q(out_5));  // open: Qn, preset, en, reset
endmodule
