// Logisim project Lab1.circ as structural Verilog
module All_Gates_using_NAND_Gate (
  input  A,
  input  B,
  output NOT_A,
  output A_AND_B,
  output A_OR_B,
  output A_NOR_B,
  output A_XOR_B
);

  wire nand_1_out, nand_2_out, nand_3_out, nand_4_out, nand_5_out, nand_6_out, nand_10_out, nand_11_out,
       nand_12_out;

  nand nand_1 (nand_1_out, A, B);
  nand nand_2 (nand_2_out, A, A);
  nand nand_3 (nand_3_out, B, B);
  nand nand_4 (nand_4_out, A, A);
  nand nand_5 (nand_5_out, B, B);
  nand nand_6 (nand_6_out, A, B);
  nand nand_7 (NOT_A, A, A);
  nand nand_8 (A_AND_B, nand_1_out, nand_1_out);
  nand nand_9 (A_OR_B, nand_2_out, nand_3_out);
  nand nand_10 (nand_10_out, nand_4_out, nand_5_out);
  nand nand_11 (nand_11_out, A, nand_6_out);
  nand nand_12 (nand_12_out, nand_6_out, B);
  nand nand_13 (A_NOR_B, nand_10_out, nand_10_out);
  nand nand_14 (A_XOR_B, nand_11_out, nand_12_out);

  // Notes on the sheet:
  //   NOT GATE
  //   AND GATE
  //   OR GATE
  //   NOR GATE
  //   XOR GATE
endmodule

// HA
module Half_Adder_1 (
  input  X,
  input  Y,
  output S,
  output C
);

  wire and_1_out, and_2_out, not_1_out, not_2_out;

  not not_1 (not_1_out, X);
  not not_2 (not_2_out, Y);
  and and_1 (and_1_out, not_1_out, Y);
  and and_2 (and_2_out, X, not_2_out);
  or or_1 (S, and_1_out, and_2_out);
  and and_3 (C, X, Y);

  // Notes on the sheet:
  //   Half Adder
endmodule

module Half_Adder_2 (
  input  X,
  input  Y,
  output S,
  output C
);

  xor xor_1 (S, X, Y);
  and and_1 (C, X, Y);

  // Notes on the sheet:
  //   Half Adder
endmodule

module Full_Adder_1 (
  input  X,
  input  Y,
  input  Z,
  output S,
  output C
);

  wire and_1_out, and_2_out, and_3_out, and_4_out, and_5_out, and_6_out, and_7_out, and_8_out, not_1_out,
       not_2_out, not_3_out, not_4_out, not_5_out, not_6_out, not_7_out, not_8_out, not_9_out;

  and and_1 (and_1_out, X, Y, Z);
  not not_1 (not_1_out, X);
  and and_2 (and_2_out, not_1_out, not_2_out, Z);
  not not_2 (not_2_out, Y);
  not not_3 (not_3_out, X);
  and and_3 (and_3_out, not_3_out, Y, not_4_out);
  not not_4 (not_4_out, Z);
  and and_4 (and_4_out, X, not_5_out, not_6_out);
  not not_5 (not_5_out, Y);
  not not_6 (not_6_out, Z);
  and and_5 (and_5_out, X, Y, Z);
  not not_7 (not_7_out, X);
  and and_6 (and_6_out, not_7_out, Y, Z);
  and and_7 (and_7_out, X, not_8_out, Z);
  not not_8 (not_8_out, Y);
  and and_8 (and_8_out, X, Y, not_9_out);
  not not_9 (not_9_out, Z);
  or or_1 (S, and_1_out, and_2_out, and_3_out, and_4_out);
  or or_2 (C, and_5_out, and_6_out, and_7_out, and_8_out);

  // Notes on the sheet:
  //   Full Adder
endmodule

module Full_Adder_2 (
  input  X,
  input  Y,
  input  Z,
  output S,
  output C
);

  wire and_1_out, and_2_out, xor_1_out;

  xor xor_1 (xor_1_out, X, Y);
  and and_1 (and_1_out, xor_1_out, Z);
  and and_2 (and_2_out, X, Y);
  xor xor_2 (S, xor_1_out, Z);
  or or_1 (C, and_1_out, and_2_out);

  // Notes on the sheet:
  //   Full Adder
endmodule

module Full_Adder_using_Half_Adder (
  input  X,
  input  Y,
  input  Z,
  output S,
  output C
);

  wire half_adder_1_1_c, half_adder_1_1_s, half_adder_1_2_c;

  Half_Adder_1 half_adder_1_1 (.X(X), .Y(Y), .S(half_adder_1_1_s), .C(half_adder_1_1_c));
  Half_Adder_1 half_adder_1_2 (.X(half_adder_1_1_s), .Y(Z), .S(S), .C(half_adder_1_2_c));
  or or_1 (C, half_adder_1_2_c, half_adder_1_1_c);

  // Notes on the sheet:
  //   Full Adder using Half Adder
endmodule
