// Logisim project Lab2.circ as structural Verilog
// FA
module Full_Adder (
  input  X,
  input  Y,
  input  Z,
  output S,
  output C
);

  wire and_1_out, and_2_out, xor_1_out;

  xor xor_1 (xor_1_out, X, Y);
  and and_1 (and_1_out, xor_1_out, Z);
  and and_2 (and_2_out, X, Y);
  xor xor_2 (S, xor_1_out, Z);
  or or_1 (C, and_1_out, and_2_out);

  // Notes on the sheet:
  //   Full Adder
endmodule

module _4_Bit_Adder (
  input  Cin,
  input  A0,
  input  B0,
  input  A1,
  input  B1,
  input  A2,
  input  B2,
  input  A3,
  input  B3,
  output S0,
  output S1,
  output S2,
  output S3,
  output Cout
);

  wire full_adder_1_c, full_adder_2_c, full_adder_3_c;

  Full_Adder full_adder_1 (.X(A0), .Y(B0), .Z(Cin), .S(S0), .C(full_adder_1_c));
  Full_Adder full_adder_2 (.X(A1), .Y(B1), .Z(full_adder_1_c), .S(S1), .C(full_adder_2_c));
  Full_Adder full_adder_3 (.X(A2), .Y(B2), .Z(full_adder_2_c), .S(S2), .C(full_adder_3_c));
  Full_Adder full_adder_4 (.X(A3), .Y(B3), .Z(full_adder_3_c), .S(S3), .C(Cout));

  // Notes on the sheet:
  //   4 Bit Adder
endmodule

module _4_Bit_Subtractor (
  input  Cin,
  input  A0,
  input  B0,
  input  A1,
  input  B1,
  input  A2,
  input  B2,
  input  A3,
  input  B3,
  output D0,
  output D1,
  output D2,
  output D3,
  output Cout
);

  wire full_adder_1_c, full_adder_2_c, full_adder_3_c, not_1_out, not_2_out, not_3_out, not_4_out;

  not not_1 (not_1_out, B0);
  not not_2 (not_2_out, B1);
  not not_3 (not_3_out, B2);
  not not_4 (not_4_out, B3);
  Full_Adder full_adder_1 (.X(A0), .Y(not_1_out), .Z(Cin), .S(D0), .C(full_adder_1_c));
  Full_Adder full_adder_2 (.X(A1), .Y(not_2_out), .Z(full_adder_1_c), .S(D1), .C(full_adder_2_c));
  Full_Adder full_adder_3 (.X(A2), .Y(not_3_out), .Z(full_adder_2_c), .S(D2), .C(full_adder_3_c));
  Full_Adder full_adder_4 (.X(A3), .Y(not_4_out), .Z(full_adder_3_c), .S(D3), .C(Cout));

  // Notes on the sheet:
  //   4 Bit Subtractor
endmodule

module _4_Bit_Parallel (
  input  M,
  input  A0,
  input  B0,
  input  A1,
  input  B1,
  input  A2,
  input  B2,
  input  A3,
  input  B3,
  output R0,
  output R1,
  output R2,
  output R3,
  output Cout
);

  wire full_adder_1_c, full_adder_2_c, full_adder_3_c, xor_1_out, xor_2_out, xor_3_out, xor_4_out;

  xor xor_1 (xor_1_out, B0, M);
  xor xor_2 (xor_2_out, B1, M);
  xor xor_3 (xor_3_out, B2, M);
  xor xor_4 (xor_4_out, B3, M);
  Full_Adder full_adder_1 (.X(A0), .Y(xor_1_out), .Z(M), .S(R0), .C(full_adder_1_c));
  Full_Adder full_adder_2 (.X(A1), .Y(xor_2_out), .Z(full_adder_1_c), .S(R1), .C(full_adder_2_c));
  Full_Adder full_adder_3 (.X(A2), .Y(xor_3_out), .Z(full_adder_2_c), .S(R2), .C(full_adder_3_c));
  Full_Adder full_adder_4 (.X(A3), .Y(xor_4_out), .Z(full_adder_3_c), .S(R3), .C(Cout));

  // Notes on the sheet:
  //   4 Bit Parallel Adder - Subtractor
endmodule
