// Logisim project Lab3.circ as structural Verilog: 9 circuits, main circuit main
module main (
  output out_1,
  output out_2,
  output out_3
);

  wire button_1_out, not_1_out, not_2_out, not_3_out;

  Button button_1 (.out(button_1_out));
  J_K_Flip_Flop j_k_ff_1 (.J(1'b1), .clk(not_1_out), .K(1'b1), .Q(out_3));  // open: Qn, preset, en, reset
  not not_1 (not_1_out, button_1_out);
  J_K_Flip_Flop j_k_ff_2 (.J(1'b1), .clk(not_2_out), .K(1'b1), .Q(out_2));  // open: Qn, preset, en, reset
  not not_2 (not_2_out, out_3);
  not not_3 (not_3_out, out_2);
  J_K_Flip_Flop j_k_ff_3 (.J(1'b1), .clk(not_3_out), .K(1'b1), .Q(out_1));  // open: Qn, preset, en, reset
endmodule

module Mod_8_Counter (
  output out_1,
  output out_2,
  output out_3
);

  wire clock_1_out, not_1_out, not_2_out, not_3_out;

  Clock clock_1 (.out(clock_1_out));
  J_K_Flip_Flop j_k_ff_1 (.J(1'b1), .clk(not_1_out), .K(1'b1), .Q(out_3));  // open: Qn, preset, en, reset
  not not_1 (not_1_out, clock_1_out);
  J_K_Flip_Flop j_k_ff_2 (.J(1'b1), .clk(not_2_out), .K(1'b1), .Q(out_2));  // open: Qn, preset, en, reset
  not not_2 (not_2_out, out_3);
  not not_3 (not_3_out, out_2);
  J_K_Flip_Flop j_k_ff_3 (.J(1'b1), .clk(not_3_out), .K(1'b1), .Q(out_1));  // open: Qn, preset, en, reset

  // Notes on the sheet:
  //   Mod 8 Counter (Asynchronous)
endmodule

module Mod_16_Counter (
  output out_1,
  output out_2,
  output out_3,
  output out_4
);

  wire clock_1_out, not_1_out, not_2_out, not_3_out, not_4_out;

  Clock clock_1 (.out(clock_1_out));
  J_K_Flip_Flop j_k_ff_1 (.J(1'b1), .clk(not_1_out), .K(1'b1), .Q(out_4));  // open: Qn, preset, en, reset
  not not_1 (not_1_out, clock_1_out);
  J_K_Flip_Flop j_k_ff_2 (.J(1'b1), .clk(not_2_out), .K(1'b1), .Q(out_3));  // open: Qn, preset, en, reset
  not not_2 (not_2_out, out_4);
  not not_3 (not_3_out, out_3);
  J_K_Flip_Flop j_k_ff_3 (.J(1'b1), .clk(not_3_out), .K(1'b1), .Q(out_2));  // open: Qn, preset, en, reset
  J_K_Flip_Flop j_k_ff_4 (.J(1'b1), .clk(not_4_out), .K(1'b1), .Q(out_1));  // open: Qn, preset, en, reset
  not not_4 (not_4_out, out_2);
endmodule

module Mod_10_Counter (
  output out_1,
  output out_2,
  output out_3,
  output out_4
);

  wire clock_1_out, nand_1_out, not_1_out, not_2_out, not_3_out, not_4_out, not_5_out, not_6_out, not_7_out,
       not_8_out, not_9_out;

  Clock clock_1 (.out(clock_1_out));
  J_K_Flip_Flop j_k_ff_1 (.J(1'b1), .clk(not_1_out), .K(1'b1), .Q(out_4), .reset(not_2_out));  // open: Qn, preset, en
  not not_1 (not_1_out, clock_1_out);
  not not_2 (not_2_out, nand_1_out);
  not not_3 (not_3_out, out_2);
  nand nand_1 (nand_1_out, out_1, not_3_out, out_3, out_4);
  J_K_Flip_Flop j_k_ff_2 (.J(1'b1), .clk(not_4_out), .K(1'b1), .Q(out_3), .reset(not_5_out));  // open: Qn, preset, en
  not not_4 (not_4_out, out_4);
  not not_5 (not_5_out, nand_1_out);
  not not_6 (not_6_out, out_3);
  J_K_Flip_Flop j_k_ff_3 (.J(1'b1), .clk(not_6_out), .K(1'b1), .Q(out_2), .reset(not_7_out));  // open: Qn, preset, en
  not not_7 (not_7_out, nand_1_out);
  J_K_Flip_Flop j_k_ff_4 (.J(1'b1), .clk(not_8_out), .K(1'b1), .Q(out_1), .reset(not_9_out));  // open: Qn, preset, en
  not not_8 (not_8_out, out_2);
  not not_9 (not_9_out, nand_1_out);

  // Notes on the sheet:
  //   1011  -->  0000
endmodule

module _2___10_Counter (
  output out_1,
  output out_2,
  output out_3,
  output out_4
);

  wire clock_1_out, nand_1_out, not_1_out, not_2_out, not_3_out, not_4_out, not_5_out, not_6_out, not_7_out,
       not_8_out, not_9_out;

  Clock clock_1 (.out(clock_1_out));
  J_K_Flip_Flop j_k_ff_1 (.J(1'b1), .clk(not_1_out), .K(1'b1), .Q(out_4), .reset(not_2_out));  // open: Qn, preset, en
  not not_1 (not_1_out, clock_1_out);
  not not_2 (not_2_out, nand_1_out);
  not not_3 (not_3_out, out_2);
  nand nand_1 (nand_1_out, out_1, not_3_out, out_3, out_4);
  J_K_Flip_Flop j_k_ff_2 (.J(1'b1), .clk(not_4_out), .K(1'b1), .Q(out_3), .preset(not_5_out));  // open: Qn, en, reset
  not not_4 (not_4_out, out_4);
  not not_5 (not_5_out, nand_1_out);
  not not_6 (not_6_out, out_3);
  J_K_Flip_Flop j_k_ff_3 (.J(1'b1), .clk(not_6_out), .K(1'b1), .Q(out_2), .reset(not_7_out));  // open: Qn, preset, en
  not not_7 (not_7_out, nand_1_out);
  J_K_Flip_Flop j_k_ff_4 (.J(1'b1), .clk(not_8_out), .K(1'b1), .Q(out_1), .reset(not_9_out));  // open: Qn, preset, en
  not not_8 (not_8_out, out_2);
  not not_9 (not_9_out, nand_1_out);

  // Notes on the sheet:
  //   1011  -->  0010
endmodule

module Mod_8_Sync_Counter (
  output out_1,
  output out_2,
  output out_3
);

  wire and_1_out, clock_1_out;

  Clock clock_1 (.out(clock_1_out));
  J_K_Flip_Flop j_k_ff_1 (.J(1'b1), .clk(clock_1_out), .K(1'b1), .Q(out_3));  // open: Qn, preset, en, reset
  J_K_Flip_Flop j_k_ff_2 (.J(out_3), .clk(clock_1_out), .K(out_3), .Q(out_2));  // open: Qn, preset, en, reset
  and and_1 (and_1_out, out_3, out_2);
  J_K_Flip_Flop j_k_ff_3 (.J(and_1_out), .clk(clock_1_out), .K(and_1_out), .Q(out_1));  // open: Qn, preset, en, reset

  // Notes on the sheet:
  //   Synchronous Counter
endmodule

module Mod_16_Sync_Counter (
  output out_1,
  output out_2,
  output out_3,
  output out_4
);

  wire and_1_out, and_2_out, clock_1_out;

  Clock clock_1 (.out(clock_1_out));
  J_K_Flip_Flop j_k_ff_1 (.J(1'b1), .clk(clock_1_out), .K(1'b1), .Q(out_4));  // open: Qn, preset, en, reset
  J_K_Flip_Flop j_k_ff_2 (.J(out_4), .clk(clock_1_out), .K(out_4), .Q(out_3));  // open: Qn, preset, en, reset
  and and_1 (and_1_out, out_4, out_3);
  J_K_Flip_Flop j_k_ff_3 (.J(and_1_out), .clk(clock_1_out), .K(and_1_out), .Q(out_2));  // open: Qn, preset, en, reset
  and and_2 (and_2_out, and_1_out, out_2);
  J_K_Flip_Flop j_k_ff_4 (.J(and_2_out), .clk(clock_1_out), .K(and_2_out), .Q(out_1));  // open: Qn, preset, en, reset
endmodule

module Mod_10_Sync_Counter (
  output out_1,
  output out_2,
  output out_3,
  output out_4
);

  wire and_1_out, and_2_out, clock_1_out, nand_1_out, not_1_out, not_2_out, not_3_out, not_4_out, not_5_out;

  Clock clock_1 (.out(clock_1_out));
  J_K_Flip_Flop j_k_ff_1 (.J(1'b1), .clk(clock_1_out), .K(1'b1), .Q(out_4), .reset(not_1_out));  // open: Qn, preset, en
  not not_1 (not_1_out, nand_1_out);
  not not_2 (not_2_out, out_2);
  nand nand_1 (nand_1_out, out_1, not_2_out, out_3, out_4);
  J_K_Flip_Flop j_k_ff_2 (
    .J(out_4), .clk(clock_1_out), .K(out_4), .Q(out_3), .reset(not_3_out));  // open: Qn, preset, en
  not not_3 (not_3_out, nand_1_out);
  and and_1 (and_1_out, out_4, out_3);
  J_K_Flip_Flop j_k_ff_3 (
    .J(and_1_out), .clk(clock_1_out), .K(and_1_out), .Q(out_2), .reset(not_4_out));  // open: Qn, preset, en
  not not_4 (not_4_out, nand_1_out);
  and and_2 (and_2_out, and_1_out, out_2);
  J_K_Flip_Flop j_k_ff_4 (
    .J(and_2_out), .clk(clock_1_out), .K(and_2_out), .Q(out_1), .reset(not_5_out));  // open: Qn, preset, en
  not not_5 (not_5_out, nand_1_out);
endmodule

module _2___10_Sync_Counter (
  output out_1,
  output out_2,
  output out_3,
  output out_4
);

  wire and_1_out, and_2_out, clock_1_out, nand_1_out, not_1_out, not_2_out, not_3_out, not_4_out, not_5_out;

  Clock clock_1 (.out(clock_1_out));
  J_K_Flip_Flop j_k_ff_1 (.J(1'b1), .clk(clock_1_out), .K(1'b1), .Q(out_4), .reset(not_1_out));  // open: Qn, preset, en
  not not_1 (not_1_out, nand_1_out);
  not not_2 (not_2_out, out_2);
  nand nand_1 (nand_1_out, out_1, not_2_out, out_3, out_4);
  J_K_Flip_Flop j_k_ff_2 (
    .J(out_4), .clk(clock_1_out), .K(out_4), .Q(out_3), .preset(not_3_out));  // open: Qn, en, reset
  not not_3 (not_3_out, nand_1_out);
  and and_1 (and_1_out, out_4, out_3);
  J_K_Flip_Flop j_k_ff_3 (
    .J(and_1_out), .clk(clock_1_out), .K(and_1_out), .Q(out_2), .reset(not_4_out));  // open: Qn, preset, en
  not not_4 (not_4_out, nand_1_out);
  and and_2 (and_2_out, and_1_out, out_2);
  J_K_Flip_Flop j_k_ff_4 (
    .J(and_2_out), .clk(clock_1_out), .K(and_2_out), .Q(out_1), .reset(not_5_out));  // open: Qn, preset, en
  not not_5 (not_5_out, nand_1_out);
endmodule
