// Logisim project Lab5.circ as structural Verilog
module Left_Shift (
  input  Serial_Input,
  output B3,
  output B2,
  output B1,
  output B0
);

  wire clock_1_out;

  Clock clock_1 (.out(clock_1_out));
  D_Flip_Flop d_ff_1 (.clk(clock_1_out), .D(B2), .Q(B3));  // open: Qn, preset, en, reset
  D_Flip_Flop d_ff_2 (.clk(clock_1_out), .D(B1), .Q(B2));  // open: Qn, preset, en, reset
  D_Flip_Flop d_ff_3 (.clk(clock_1_out), .D(B0), .Q(B1));  // open: Qn, preset, en, reset
  D_Flip_Flop d_ff_4 (.clk(clock_1_out), .D(Serial_Input), .Q(B0));  // open: Qn, preset, en, reset
endmodule

module Right_Shift (
  input  Serial_Input,
  output B3,
  output B2,
  output B1,
  output B0
);

  wire clock_1_out;

  Clock clock_1 (.out(clock_1_out));
  D_Flip_Flop d_ff_1 (.clk(clock_1_out), .D(Serial_Input), .Q(B3));  // open: Qn, preset, en, reset
  D_Flip_Flop d_ff_2 (.clk(clock_1_out), .D(B3), .Q(B2));  // open: Qn, preset, en, reset
  D_Flip_Flop d_ff_3 (.clk(clock_1_out), .D(B2), .Q(B1));  // open: Qn, preset, en, reset
  D_Flip_Flop d_ff_4 (.clk(clock_1_out), .D(B1), .Q(B0));  // open: Qn, preset, en, reset
endmodule

module Universal_Shift (
  input  [1:0] in_1,
  input  Serial_Input_for_Right_Shift,
  input  Serial_Input_for_Left_Shift,
  input  in_4,
  input  in_5,
  input  in_6,
  input  in_7,
  output A3,
  output A2,
  output A1,
  output A0
);

  wire clock_1_out, multiplexer_1_out, multiplexer_2_out, multiplexer_3_out, multiplexer_4_out;

  Clock clock_1 (.out(clock_1_out));
  Multiplexer #(.select(2), .enable("false")) multiplexer_1 (
    .in0(A3), .in1(A0), .in2(Serial_Input_for_Right_Shift), .in3(in_4), .out(multiplexer_1_out), .sel(in_1));
  D_Flip_Flop d_ff_1 (.clk(clock_1_out), .D(multiplexer_1_out), .Q(A3));  // open: Qn, preset, en, reset
  Multiplexer #(.select(2), .enable("false")) multiplexer_2 (
    .in0(A0), .in1(A1), .in2(A3), .in3(in_5), .out(multiplexer_2_out), .sel(in_1));
  D_Flip_Flop d_ff_2 (.clk(clock_1_out), .D(multiplexer_2_out), .Q(A0));  // open: Qn, preset, en, reset
  D_Flip_Flop d_ff_3 (.clk(clock_1_out), .D(multiplexer_3_out), .Q(A1));  // open: Qn, preset, en, reset
  Multiplexer #(.select(2), .enable("false")) multiplexer_3 (
    .in0(A1), .in1(A0), .in2(A0), .in3(in_6), .out(multiplexer_3_out), .sel(in_1));
  Multiplexer #(.select(2), .enable("false")) multiplexer_4 (
    .in0(A0), .in1(Serial_Input_for_Left_Shift), .in2(A1), .in3(in_7), .out(multiplexer_4_out), .sel(in_1));
  D_Flip_Flop d_ff_4 (.clk(clock_1_out), .D(multiplexer_4_out), .Q(A0));  // open: Qn, preset, en, reset

  assign A2 = A0;
endmodule

module Universal_Shift_2 (
  input  serial_input,
  input  in_2,
  input  in_3,
  input  in_4,
  input  in_5,
  input  serial_input_2,
  input  [1:0] in_7,
  output out_8,
  output out_9,
  output out_10,
  output out_11
);

  wire clock_1_out, multiplexer_1_out, multiplexer_2_out, multiplexer_3_out, multiplexer_4_out;

  Clock clock_1 (.out(clock_1_out));
  Multiplexer #(.select(2)) multiplexer_1 (
    .in0(out_8), .in1(serial_input), .in2(out_9), .in3(in_2), .out(multiplexer_1_out), .sel(in_7));  // open: en
  Multiplexer #(.select(2)) multiplexer_2 (
    .in0(out_9), .in1(out_8), .in2(out_10), .in3(in_3), .out(multiplexer_2_out), .sel(in_7));  // open: en
  Multiplexer #(.select(2)) multiplexer_3 (
    .in0(out_10), .in1(out_9), .in2(out_11), .in3(in_4), .out(multiplexer_3_out), .sel(in_7));  // open: en
  Multiplexer #(.select(2)) multiplexer_4 (
    .in0(out_11), .in1(out_10), .in2(serial_input_2), .in3(in_5), .out(multiplexer_4_out), .sel(in_7));  // open: en
  D_Flip_Flop d_ff_1 (.clk(clock_1_out), .D(multiplexer_1_out), .Q(out_8));  // open: Qn, preset, en, reset
  D_Flip_Flop d_ff_2 (.clk(clock_1_out), .D(multiplexer_2_out), .Q(out_9));  // open: Qn, preset, en, reset
  D_Flip_Flop d_ff_3 (.clk(clock_1_out), .D(multiplexer_3_out), .Q(out_10));  // open: Qn, preset, en, reset
  D_Flip_Flop d_ff_4 (.clk(clock_1_out), .D(multiplexer_4_out), .Q(out_11));  // open: Qn, preset, en, reset
endmodule

module Arithmetic_Left_Shift (
  input  in_1,
  input  in_2,
  input  in_3,
  input  in_4,
  output B3,
  output B2,
  output B1,
  output B0
);

  wire button_1_out;

  Button button_1 (.out(button_1_out));
  D_Flip_Flop d_ff_1 (.clk(button_1_out), .D(in_2), .Q(B3));  // open: Qn, preset, en, reset
  D_Flip_Flop d_ff_2 (.clk(button_1_out), .D(in_3), .Q(B2));  // open: Qn, preset, en, reset
  D_Flip_Flop d_ff_3 (.clk(button_1_out), .D(in_4), .Q(B1));  // open: Qn, preset, en, reset
  D_Flip_Flop d_ff_4 (.clk(button_1_out), .D(1'b0), .Q(B0));  // open: Qn, preset, en, reset

  // Notes on the sheet:
  //   MSB
  //   LSB
endmodule

module Arithmetic_Right_Shift (
  input  in_1,
  input  in_2,
  input  in_3,
  input  in_4,
  output B3,
  output B2,
  output B1,
  output B0
);

  wire clock_1_out;

  Clock clock_1 (.out(clock_1_out));
  D_Flip_Flop d_ff_1 (.clk(clock_1_out), .D(in_1), .Q(B3));  // open: Qn, preset, en, reset
  D_Flip_Flop d_ff_2 (.clk(clock_1_out), .D(in_1), .Q(B2));  // open: Qn, preset, en, reset
  D_Flip_Flop d_ff_3 (.clk(clock_1_out), .D(in_2), .Q(B1));  // open: Qn, preset, en, reset
  D_Flip_Flop d_ff_4 (.clk(clock_1_out), .D(in_3), .Q(B0));  // open: Qn, preset, en, reset

  // Notes on the sheet:
  //   MSB
  //   LSB
endmodule

module Logical_Left_Shift (
  input  in_1,
  input  in_2,
  input  in_3,
  output B3,
  output B2,
  output B1,
  output B0
);

  wire button_1_out;

  Button button_1 (.out(button_1_out));
  D_Flip_Flop d_ff_1 (.clk(button_1_out), .D(in_1), .Q(B3));  // open: Qn, preset, en, reset
  D_Flip_Flop d_ff_2 (.clk(button_1_out), .D(in_2), .Q(B2));  // open: Qn, preset, en, reset
  D_Flip_Flop d_ff_3 (.clk(button_1_out), .D(in_3), .Q(B1));  // open: Qn, preset, en, reset
  D_Flip_Flop d_ff_4 (.clk(button_1_out), .D(1'b0), .Q(B0));  // open: Qn, preset, en, reset

  // Notes on the sheet:
  //   MSB
  //   LSB
endmodule

module Logical_Right_Shift (
  input  in_1,
  input  in_2,
  input  in_3,
  input  in_4,
  output B3,
  output B2,
  output B1,
  output B0
);

  wire clock_1_out;

  Clock clock_1 (.out(clock_1_out));
  D_Flip_Flop d_ff_1 (.clk(clock_1_out), .D(1'b0), .Q(B3));  // open: Qn, preset, en, reset
  D_Flip_Flop d_ff_2 (.clk(clock_1_out), .D(in_1), .Q(B2));  // open: Qn, preset, en, reset
  D_Flip_Flop d_ff_3 (.clk(clock_1_out), .D(in_2), .Q(B1));  // open: Qn, preset, en, reset
  D_Flip_Flop d_ff_4 (.clk(clock_1_out), .D(in_3), .Q(B0));  // open: Qn, preset, en, reset

  // Notes on the sheet:
  //   MSB
  //   LSB
endmodule
