// Logisim project Practice1.circ as structural Verilog
module Full_Adder (
  input  X,
  input  Y,
  input  Z,
  output S,
  output C
);

  wire and_1_out, and_2_out, xor_1_out;

  xor xor_1 (xor_1_out, X, Y);
  and and_1 (and_1_out, xor_1_out, Z);
  and and_2 (and_2_out, X, Y);
  xor xor_2 (S, xor_1_out, Z);
  or or_1 (C, and_1_out, and_2_out);

  // Notes on the sheet:
  //   Full Adder
endmodule

module _4_Bit_Adder_Subtractor (
  input  M,
  input  A3,
  input  A2,
  input  A1,
  input  A0,
  input  B3,
  input  B2,
  input  B1,
  input  B0,
  output Cout,
  output R3,
  output R2,
  output R1,
  output R0
);

  wire full_adder_1_c, full_adder_2_c, full_adder_3_c, xor_1_out, xor_2_out, xor_3_out, xor_4_out;

  xor xor_1 (xor_1_out, B0, M);
  xor xor_2 (xor_2_out, B1, M);
  xor xor_3 (xor_3_out, B2, M);
  xor xor_4 (xor_4_out, B3, M);
  Full_Adder full_adder_1 (.X(A0), .Y(xor_1_out), .Z(M), .S(R0), .C(full_adder_1_c));
  Full_Adder full_adder_2 (.X(A1), .Y(xor_2_out), .Z(full_adder_1_c), .S(R1), .C(full_adder_2_c));
  Full_Adder full_adder_3 (.X(A2), .Y(xor_3_out), .Z(full_adder_2_c), .S(R2), .C(full_adder_3_c));
  Full_Adder full_adder_4 (.X(A3), .Y(xor_4_out), .Z(full_adder_3_c), .S(R3), .C(Cout));

  // Notes on the sheet:
  //   4 Bit Parallel Adder - Subtractor
endmodule
