// Logisim project Sequential.circ as structural Verilog
module Latch_1 (
  input  in_1,
  input  in_2,
  output out_3,
  output out_4
);

  nor nor_1 (out_3, in_1, out_4);
  nor nor_2 (out_4, out_3, in_2);
endmodule

module Latch_2 (
  input  in_1,
  input  in_2,
  output out_3,
  output out_4
);

  nand nand_1 (out_3, in_1, out_4);
  nand nand_2 (out_4, out_3, in_2);
endmodule

module S_R_Flip_Flop (
  input  in_1,
  input  in_2,
  output out_3,
  output out_4
);

  wire clock_1_out, nand_1_out, nand_2_out;

  Clock clock_1 (.out(clock_1_out));
  nand nand_1 (nand_1_out, in_1, clock_1_out);
  nand nand_2 (nand_2_out, clock_1_out, in_2);
  nand nand_3 (out_3, nand_1_out, out_4);
  nand nand_4 (out_4, out_3, nand_2_out);
endmodule

module D_Flip_Flop (
  input  in_1,
  output out_2,
  output out_3
);

  wire clock_1_out, nand_1_out, nand_2_out, not_1_out;

  Clock clock_1 (.out(clock_1_out));
  not not_1 (not_1_out, in_1);
  nand nand_1 (nand_1_out, in_1, clock_1_out);
  nand nand_2 (nand_2_out, clock_1_out, not_1_out);
  nand nand_3 (out_2, nand_1_out, out_3);
  nand nand_4 (out_3, out_2, nand_2_out);
endmodule

module J_K_Flip_Flop (
  input  in_1,
  input  in_2,
  output out_3,
  output out_4
);

  wire clock_1_out, nand_1_out, nand_2_out;

  Clock clock_1 (.out(clock_1_out));
  nand nand_1 (nand_1_out, out_4, in_1, clock_1_out);
  nand nand_2 (nand_2_out, clock_1_out, in_2, out_3);
  nand nand_3 (out_3, nand_1_out, out_4);
  nand nand_4 (out_4, out_3, nand_2_out);
endmodule

module J_K_Master_Slave (
  input  in_1,
  input  in_2,
  output out_3,
  output out_4
);

  wire clock_1_out, nand_1_out, nand_2_out, nand_3_out, nand_4_out, nand_5_out, nand_6_out, not_1_out;

  Clock clock_1 (.out(clock_1_out));
  nand nand_1 (nand_1_out, out_4, in_1, clock_1_out);
  nand nand_2 (nand_2_out, clock_1_out, in_2, out_3);
  not not_1 (not_1_out, clock_1_out);
  nand nand_3 (nand_3_out, nand_1_out, nand_4_out);
  nand nand_4 (nand_4_out, nand_3_out, nand_2_out);
  nand nand_5 (nand_5_out, not_1_out, nand_3_out);
  nand nand_6 (nand_6_out, nand_4_out, not_1_out);
  nand nand_7 (out_3, nand_5_out, out_4);
  nand nand_8 (out_4, out_3, nand_6_out);
endmodule

module T_Flip_Flop (
  input  in_1,
  output out_2,
  output out_3
);

  wire clock_1_out, nand_1_out, nand_2_out, nand_3_out, nand_4_out, nand_5_out, nand_6_out, not_1_out;

  Clock clock_1 (.out(clock_1_out));
  nand nand_1 (nand_1_out, out_3, in_1, clock_1_out);
  nand nand_2 (nand_2_out, clock_1_out, in_1, out_2);
  not not_1 (not_1_out, clock_1_out);
  nand nand_3 (nand_3_out, nand_1_out, nand_4_out);
  nand nand_4 (nand_4_out, nand_3_out, nand_2_out);
  nand nand_5 (nand_5_out, not_1_out, nand_3_out);
  nand nand_6 (nand_6_out, nand_4_out, not_1_out);
  nand nand_7 (out_2, nand_5_out, out_3);
  nand nand_8 (out_3, out_2, nand_6_out);
endmodule

module Counter (
  input  in_1,
  input  in_2,
  input  in_3,
  output out_4,
  output out_5,
  output out_6
);

  wire nand_1_out, not_1_out, not_2_out, not_3_out, not_4_out, not_5_out, not_6_out, not_7_out;

  J_K_Flip_Flop_part j_k_ff_1 (
    .J(in_1), .clk(not_1_out), .K(in_3), .Q(out_6), .reset(not_2_out));  // open: Qn, preset, en
  not not_1 (not_1_out, in_2);
  not not_2 (not_2_out, nand_1_out);
  not not_3 (not_3_out, out_6);
  J_K_Flip_Flop_part j_k_ff_2 (
    .J(in_1), .clk(not_4_out), .K(in_3), .Q(out_5), .preset(not_5_out));  // open: Qn, en, reset
  not not_4 (not_4_out, out_6);
  not not_5 (not_5_out, nand_1_out);
  nand nand_1 (nand_1_out, out_4, out_5, not_3_out);
  not not_6 (not_6_out, out_5);
  J_K_Flip_Flop_part j_k_ff_3 (
    .J(in_1), .clk(not_6_out), .K(in_3), .Q(out_4), .reset(not_7_out));  // open: Qn, preset, en
  not not_7 (not_7_out, nand_1_out);

  // Notes on the sheet:
  //   2 to 5 Counter
endmodule

module Synchronous_Counter (
  input  in_1,
  input  in_2,
  input  in_3,
  output out_4,
  output out_5,
  output out_6
);

  wire and_1_out, nand_1_out, not_1_out, not_2_out, not_3_out, not_4_out, not_5_out, not_6_out, not_7_out;

  J_K_Flip_Flop_part j_k_ff_1 (
    .J(in_1), .clk(not_1_out), .K(in_3), .Q(out_6), .reset(not_2_out));  // open: Qn, preset, en
  not not_1 (not_1_out, in_2);
  not not_2 (not_2_out, nand_1_out);
  not not_3 (not_3_out, out_6);
  not not_4 (not_4_out, in_2);
  J_K_Flip_Flop_part j_k_ff_2 (
    .J(out_6), .clk(not_4_out), .K(out_6), .Q(out_5), .preset(not_5_out));  // open: Qn, en, reset
  not not_5 (not_5_out, nand_1_out);
  nand nand_1 (nand_1_out, out_4, out_5, not_3_out);
  and and_1 (and_1_out, out_6, out_5);
  not not_6 (not_6_out, in_2);
  J_K_Flip_Flop_part j_k_ff_3 (
    .J(and_1_out), .clk(not_6_out), .K(and_1_out), .Q(out_4), .reset(not_7_out));  // open: Qn, preset, en
  not not_7 (not_7_out, nand_1_out);

  // Notes on the sheet:
  //   2 to 5 Counter
endmodule

module Register (
  input  in_1,
  input  in_2,
  input  in_3,
  input  in_4,
  input  in_5,
  output out_6,
  output out_7,
  output out_8,
  output out_9
);

  D_Flip_Flop_part d_ff_1 (.clk(in_1), .D(in_2), .Q(out_6));  // open: Qn, preset, en, reset
  D_Flip_Flop_part d_ff_2 (.clk(in_1), .D(in_3), .Q(out_7));  // open: Qn, preset, en, reset
  D_Flip_Flop_part d_ff_3 (.clk(in_1), .D(in_4), .Q(out_8));  // open: Qn, preset, en, reset
  D_Flip_Flop_part d_ff_4 (.clk(in_1), .D(in_5), .Q(out_9));  // open: Qn, preset, en, reset
endmodule

module Shift_Register (
  input  in_1,
  output out_2
);

  wire clock_1_out, d_ff_1_q, d_ff_2_q, d_ff_3_q;

  Clock clock_1 (.out(clock_1_out));
  D_Flip_Flop_part d_ff_1 (.clk(clock_1_out), .D(in_1), .Q(d_ff_1_q));  // open: Qn, preset, en, reset
  D_Flip_Flop_part d_ff_2 (.clk(clock_1_out), .D(d_ff_1_q), .Q(d_ff_2_q));  // open: Qn, preset, en, reset
  D_Flip_Flop_part d_ff_3 (.clk(clock_1_out), .D(d_ff_2_q), .Q(d_ff_3_q));  // open: Qn, preset, en, reset
  D_Flip_Flop_part d_ff_4 (.clk(clock_1_out), .D(d_ff_3_q), .Q(out_2));  // open: Qn, preset, en, reset
endmodule

module Pseudo_Random_Generator (
  output out_1,
  output out_2,
  output out_3,
  output out_4
);

  wire clock_1_out, xor_1_out;

  Clock clock_1 (.out(clock_1_out));
  D_Flip_Flop_part d_ff_1 (.clk(clock_1_out), .D(xor_1_out), .Q(out_1));  // open: Qn, preset, en, reset
  D_Flip_Flop_part d_ff_2 (.clk(clock_1_out), .D(out_1), .Q(out_2));  // open: Qn, preset, en, reset
  D_Flip_Flop_part d_ff_3 (.clk(clock_1_out), .D(out_2), .Q(out_3));  // open: Qn, preset, en, reset
  xor xor_1 (xor_1_out, out_3, out_4);
  D_Flip_Flop_part d_ff_4 (.clk(clock_1_out), .D(out_3), .Q(out_4));  // open: Qn, preset, en, reset
endmodule

module Multi_Phase_CLocks (
  output out_1,
  output out_2,
  output out_3
);

  wire clock_1_out, j_k_ff_1_qn, j_k_ff_2_qn, j_k_ff_3_qn;

  Clock clock_1 (.out(clock_1_out));
  J_K_Flip_Flop_part j_k_ff_1 (
    .J(j_k_ff_3_qn), .clk(clock_1_out), .K(out_3), .Q(out_1), .Qn(j_k_ff_1_qn));  // open: preset, en, reset
  J_K_Flip_Flop_part j_k_ff_2 (
    .J(out_1), .clk(clock_1_out), .K(j_k_ff_1_qn), .Q(out_2), .Qn(j_k_ff_2_qn));  // open: preset, en, reset
  J_K_Flip_Flop_part j_k_ff_3 (
    .J(out_2), .clk(clock_1_out), .K(j_k_ff_2_qn), .Q(out_3), .Qn(j_k_ff_3_qn));  // open: preset, en, reset
endmodule

module Lighting (
  output out_1,
  output out_2,
  output out_3,
  output out_4,
  output out_5,
  output out_6
);

  wire clock_1_out, j_k_ff_1_q, j_k_ff_1_qn, j_k_ff_2_q, j_k_ff_2_qn, j_k_ff_3_q, j_k_ff_3_qn, not_1_out,
       not_2_out, not_3_out;

  Clock clock_1 (.out(clock_1_out));
  J_K_Flip_Flop_part j_k_ff_1 (
    .J(j_k_ff_3_qn), .clk(clock_1_out), .K(j_k_ff_3_q), .Q(j_k_ff_1_q), .Qn(j_k_ff_1_qn));  // open: preset, en, reset
  not not_1 (not_1_out, j_k_ff_1_q);
  J_K_Flip_Flop_part j_k_ff_2 (
    .J(j_k_ff_1_q), .clk(clock_1_out), .K(j_k_ff_1_qn), .Q(j_k_ff_2_q), .Qn(j_k_ff_2_qn));  // open: preset, en, reset
  not not_2 (not_2_out, j_k_ff_2_q);
  J_K_Flip_Flop_part j_k_ff_3 (
    .J(j_k_ff_2_q), .clk(clock_1_out), .K(j_k_ff_2_qn), .Q(j_k_ff_3_q), .Qn(j_k_ff_3_qn));  // open: preset, en, reset
  not not_3 (not_3_out, j_k_ff_3_q);
  and and_1 (out_1, not_1_out, not_3_out);
  and and_2 (out_2, j_k_ff_1_q, not_2_out);
  and and_3 (out_3, j_k_ff_2_q, not_3_out);
  and and_4 (out_4, j_k_ff_1_q, j_k_ff_3_q);
  and and_5 (out_5, not_1_out, j_k_ff_2_q);
  and and_6 (out_6, not_2_out, j_k_ff_3_q);
endmodule
